// Digital circuit ALU(32bits).dig as structural Verilog
module ALU_32bits (
  input  [31:0] InA,
  input  [31:0] InB,
  input  [3:0] Sel,
  output C1,
  output C2,
  output [31:0] Out
);

  wire [31:0] Add_s, and_1_out, or_1_out, Sub_s, xor_1_out;

  Add #(.Bits(32)) Add (.a(InA), .b(InB), .c_i(1'b0), .s(Add_s), .c_o(C1));
  assign xor_1_out = InA ^ InB;  // XOr xor_1, 32 bits wide
  assign and_1_out = InA & InB;  // And and_1, 32 bits wide
  assign or_1_out = InA | InB;  // Or or_1, 32 bits wide
  Sub #(.Bits(32)) Sub (.a(InA), .b(InB), .c_i(1'b0), .s(Sub_s), .c_o(C2));
  Multiplexer #(.Selector_Bits(4), .Bits(32)) multiplexer_1 (
    .sel(Sel), .in_0(Add_s), .in_1(32'h51100), .in_2(32'h57100), .in_3(32'h57400), .in_4(xor_1_out),
    .in_5(32'h51700), .in_6(and_1_out), .in_7(or_1_out), .in_8(Sub_s), .in_9({32{1'b0}}), .in_10({32{1'b0}}),
    .in_11({32{1'b0}}), .in_12({32{1'b0}}), .in_13(32'h517300), .in_14({32{1'b0}}), .in_15({32{1'b0}}),
    .out(Out));

  // Notes on the sheet:
  //   InA: Entrada 1 para cualquier operación que se vaya a realizar
  //   InB: Entrada 2 para la operación que se vaya a realizar
  //   C1: Almacena el acarreo de una suma
  //   C2: Acarreo para la resta
  //   Sel: Permite seleccionar la operación que se quiere realizar
  //   Out: Salida dependiendo de la operación escogida
  //   A<B(U)
  //   A>>>B
  //   A<<B
  //   A<B
  //   A>>B
endmodule
